# Fritzing sketch Circuit_v1 (saved by Fritzing 0.9.2b)

parts:
  RF1 = nRF8001 Bluetooth LE Breakout
  Part1 = Arduino Leonardo (Rev3b)
  J1 = Basic Force Sensing Resistor (FSR) [package=THT]
  R1 = Resistor [tolerance=±5% resistance=10k package="0805 [SMD]"]
  BATT1 = LiPoly Battery (1300mAh)
  J2 = Basic Servo

nets:
  N1: RF1.REQ, Part1.D8/A8
  N2: RF1.RDY, Part1.D7
  N3: Part1.5V, J1.pin_0
  GND: Part1.GND, Part1.A0, R1.Pin_1, BATT1.negative, J2.gnd
  N4: Part1.VIN, BATT1.positive
  N5: Part1.D9_PWM/A9, J2.pulse
  N6: Part1.D11_PWM, J2.vcc
  N7: J1.pin_1, R1.Pin_0

custom parts:
  nRF8001 Bluetooth LE Breakout: nRF8001 Breakout Board
  LiPoly Battery (1300mAh): Lithium Ion Polymer Battery (1300mAh)
